// Logisim project ALU.circ as structural Verilog: 4 circuits, main circuit halfadder
module halfadder (
  input  A,
  input  B,
  output Sum,
  output C_out
);

  xor xor_1 (Sum, A, B);
  and and_1 (C_out, A, B);
endmodule

module fulladder (
  input  A,
  input  B,
  input  C_in,
  output S_b,
  output C_out_b
);

  wire transistor_1_out, transistor_2_out, transistor_7_out, transistor_10_out, transistor_11_out,
       transistor_14_out, transistor_19_out, transistor_20_out, transistor_23_out, transistor_24_out;

  Transistor transistor_1 (.in(1'b1), .out(transistor_1_out), .gate(A));
  Transistor #(.\type ("n")) transistor_2 (.in(1'b0), .out(transistor_2_out), .gate(A));
  Transistor transistor_3 (.in(1'b1), .out(transistor_1_out), .gate(B));
  Transistor transistor_4 (.in(transistor_1_out), .out(C_out_b), .gate(C_in));
  Transistor #(.\type ("n")) transistor_5 (.in(transistor_2_out), .out(C_out_b), .gate(C_in));
  Transistor #(.\type ("n")) transistor_6 (.in(1'b0), .out(transistor_2_out), .gate(B));
  Transistor transistor_7 (.in(1'b1), .out(transistor_7_out), .gate(B));
  Transistor transistor_8 (.in(transistor_7_out), .out(C_out_b), .gate(A));
  Transistor #(.\type ("n")) transistor_9 (.in(transistor_10_out), .out(C_out_b), .gate(A));
  Transistor #(.\type ("n")) transistor_10 (.in(1'b0), .out(transistor_10_out), .gate(B));
  Transistor transistor_11 (.in(1'b1), .out(transistor_11_out), .gate(A));
  Transistor transistor_12 (.in(transistor_11_out), .out(S_b), .gate(C_out_b));
  Transistor #(.\type ("n")) transistor_13 (.in(transistor_14_out), .out(S_b), .gate(C_out_b));
  Transistor #(.\type ("n")) transistor_14 (.in(1'b0), .out(transistor_14_out), .gate(A));
  Transistor transistor_15 (.in(1'b1), .out(transistor_11_out), .gate(B));
  Transistor #(.\type ("n")) transistor_16 (.in(1'b0), .out(transistor_14_out), .gate(B));
  Transistor transistor_17 (.in(1'b1), .out(transistor_11_out), .gate(C_in));
  Transistor #(.\type ("n")) transistor_18 (.in(1'b0), .out(transistor_14_out), .gate(C_in));
  Transistor transistor_19 (.in(1'b1), .out(transistor_19_out), .gate(A));
  Transistor transistor_20 (.in(transistor_19_out), .out(transistor_20_out), .gate(B));
  Transistor transistor_21 (.in(transistor_20_out), .out(S_b), .gate(C_in));
  Transistor #(.\type ("n")) transistor_22 (.in(transistor_23_out), .out(S_b), .gate(C_in));
  Transistor #(.\type ("n")) transistor_23 (.in(transistor_24_out), .out(transistor_23_out), .gate(A));
  Transistor #(.\type ("n")) transistor_24 (.in(1'b0), .out(transistor_24_out), .gate(B));

  // Other names for the same wires on the sheet: C = C_in
endmodule

module add_sub (
  input  [31:0] A,
  input  [31:0] B,
  input  k,
  input  en_b,
  output [31:0] Y,
  output Overflow
);

  wire fulladder_1_c_out_b, fulladder_2_c_out_b, fulladder_3_c_out_b, fulladder_4_c_out_b,
       fulladder_5_c_out_b, fulladder_6_c_out_b, fulladder_7_c_out_b, fulladder_8_c_out_b,
       fulladder_9_c_out_b, fulladder_10_c_out_b, fulladder_11_c_out_b, fulladder_12_c_out_b,
       fulladder_13_c_out_b, fulladder_14_c_out_b, fulladder_15_c_out_b, fulladder_16_c_out_b,
       fulladder_17_c_out_b, fulladder_18_c_out_b, fulladder_19_c_out_b, fulladder_20_c_out_b,
       fulladder_21_c_out_b, fulladder_22_c_out_b, fulladder_23_c_out_b, fulladder_24_c_out_b,
       fulladder_25_c_out_b, fulladder_26_c_out_b, fulladder_27_c_out_b, fulladder_28_c_out_b,
       fulladder_29_c_out_b, fulladder_30_c_out_b, fulladder_31_c_out_b, fulladder_32_c_out_b, not_1_out,
       not_2_out, not_3_out, not_4_out, not_5_out, not_6_out, not_7_out, not_8_out, not_9_out, not_10_out,
       not_11_out, not_12_out, not_13_out, not_14_out, not_15_out, not_16_out, not_17_out, not_18_out,
       not_19_out, not_20_out, not_21_out, not_22_out, not_23_out, not_24_out, not_25_out, not_26_out,
       not_27_out, not_28_out, not_29_out, not_30_out, not_31_out, not_32_out, xor_1_out, xor_2_out,
       xor_3_out, xor_4_out, xor_5_out, xor_6_out, xor_7_out, xor_8_out, xor_9_out, xor_10_out, xor_11_out,
       xor_12_out, xor_13_out, xor_14_out, xor_15_out, xor_16_out, xor_17_out, xor_18_out, xor_19_out,
       xor_20_out, xor_21_out, xor_22_out, xor_23_out, xor_24_out, xor_25_out, xor_26_out, xor_27_out,
       xor_28_out, xor_29_out, xor_30_out, xor_31_out, xor_32_out, xor_33_out;
  wire [31:0] fulladder_1_s_b, not_33_out;

  xor xor_1 (xor_1_out, k, B[0]);
  xor xor_2 (xor_2_out, k, B[1]);
  xor xor_3 (xor_3_out, k, B[2]);
  xor xor_4 (xor_4_out, k, B[3]);
  xor xor_5 (xor_5_out, k, B[4]);
  xor xor_6 (xor_6_out, k, B[5]);
  xor xor_7 (xor_7_out, k, B[6]);
  xor xor_8 (xor_8_out, k, B[7]);
  xor xor_9 (xor_9_out, k, B[8]);
  xor xor_10 (xor_10_out, k, B[9]);
  xor xor_11 (xor_11_out, k, B[10]);
  xor xor_12 (xor_12_out, k, B[11]);
  xor xor_13 (xor_13_out, k, B[12]);
  xor xor_14 (xor_14_out, k, B[13]);
  xor xor_15 (xor_15_out, k, B[14]);
  xor xor_16 (xor_16_out, k, B[15]);
  xor xor_17 (xor_17_out, k, B[16]);
  xor xor_18 (xor_18_out, k, B[17]);
  xor xor_19 (xor_19_out, k, B[18]);
  xor xor_20 (xor_20_out, k, B[19]);
  xor xor_21 (xor_21_out, k, B[20]);
  xor xor_22 (xor_22_out, k, B[21]);
  xor xor_23 (xor_23_out, k, B[22]);
  xor xor_24 (xor_24_out, k, B[23]);
  xor xor_25 (xor_25_out, k, B[24]);
  xor xor_26 (xor_26_out, k, B[25]);
  xor xor_27 (xor_27_out, k, B[26]);
  xor xor_28 (xor_28_out, k, B[27]);
  xor xor_29 (xor_29_out, k, B[28]);
  xor xor_30 (xor_30_out, k, B[29]);
  xor xor_31 (xor_31_out, k, B[30]);
  xor xor_32 (xor_32_out, k, B[31]);
  fulladder fulladder_1 (.A(A[0]), .B(xor_1_out), .C_in(k), .C_out_b(fulladder_1_c_out_b), .S_b(fulladder_1_s_b[0]));
  not not_1 (not_1_out, fulladder_1_c_out_b);
  fulladder fulladder_2 (
    .A(A[1]), .B(xor_2_out), .C_in(not_1_out), .C_out_b(fulladder_2_c_out_b), .S_b(fulladder_1_s_b[1]));
  not not_2 (not_2_out, fulladder_2_c_out_b);
  fulladder fulladder_3 (
    .A(A[2]), .B(xor_3_out), .C_in(not_2_out), .C_out_b(fulladder_3_c_out_b), .S_b(fulladder_1_s_b[2]));
  not not_3 (not_3_out, fulladder_3_c_out_b);
  fulladder fulladder_4 (
    .A(A[3]), .B(xor_4_out), .C_in(not_3_out), .C_out_b(fulladder_4_c_out_b), .S_b(fulladder_1_s_b[3]));
  not not_4 (not_4_out, fulladder_4_c_out_b);
  fulladder fulladder_5 (
    .A(A[4]), .B(xor_5_out), .C_in(not_4_out), .C_out_b(fulladder_5_c_out_b), .S_b(fulladder_1_s_b[4]));
  not not_5 (not_5_out, fulladder_5_c_out_b);
  fulladder fulladder_6 (
    .A(A[5]), .B(xor_6_out), .C_in(not_5_out), .C_out_b(fulladder_6_c_out_b), .S_b(fulladder_1_s_b[5]));
  not not_6 (not_6_out, fulladder_6_c_out_b);
  fulladder fulladder_7 (
    .A(A[6]), .B(xor_7_out), .C_in(not_6_out), .C_out_b(fulladder_7_c_out_b), .S_b(fulladder_1_s_b[6]));
  not not_7 (not_7_out, fulladder_7_c_out_b);
  fulladder fulladder_8 (
    .A(A[7]), .B(xor_8_out), .C_in(not_7_out), .C_out_b(fulladder_8_c_out_b), .S_b(fulladder_1_s_b[7]));
  not not_8 (not_8_out, fulladder_8_c_out_b);
  fulladder fulladder_9 (
    .A(A[8]), .B(xor_9_out), .C_in(not_8_out), .C_out_b(fulladder_9_c_out_b), .S_b(fulladder_1_s_b[8]));
  not not_9 (not_9_out, fulladder_9_c_out_b);
  fulladder fulladder_10 (
    .A(A[9]), .B(xor_10_out), .C_in(not_9_out), .C_out_b(fulladder_10_c_out_b), .S_b(fulladder_1_s_b[9]));
  not not_10 (not_10_out, fulladder_10_c_out_b);
  fulladder fulladder_11 (
    .A(A[10]), .B(xor_11_out), .C_in(not_10_out), .C_out_b(fulladder_11_c_out_b), .S_b(fulladder_1_s_b[10]));
  not not_11 (not_11_out, fulladder_11_c_out_b);
  fulladder fulladder_12 (
    .A(A[11]), .B(xor_12_out), .C_in(not_11_out), .C_out_b(fulladder_12_c_out_b), .S_b(fulladder_1_s_b[11]));
  not not_12 (not_12_out, fulladder_12_c_out_b);
  fulladder fulladder_13 (
    .A(A[12]), .B(xor_13_out), .C_in(not_12_out), .C_out_b(fulladder_13_c_out_b), .S_b(fulladder_1_s_b[12]));
  not not_13 (not_13_out, fulladder_13_c_out_b);
  fulladder fulladder_14 (
    .A(A[13]), .B(xor_14_out), .C_in(not_13_out), .C_out_b(fulladder_14_c_out_b), .S_b(fulladder_1_s_b[13]));
  not not_14 (not_14_out, fulladder_14_c_out_b);
  fulladder fulladder_15 (
    .A(A[14]), .B(xor_15_out), .C_in(not_14_out), .C_out_b(fulladder_15_c_out_b), .S_b(fulladder_1_s_b[14]));
  not not_15 (not_15_out, fulladder_15_c_out_b);
  fulladder fulladder_16 (
    .A(A[15]), .B(xor_16_out), .C_in(not_15_out), .C_out_b(fulladder_16_c_out_b), .S_b(fulladder_1_s_b[15]));
  not not_16 (not_16_out, fulladder_16_c_out_b);
  fulladder fulladder_17 (
    .A(A[16]), .B(xor_17_out), .C_in(not_16_out), .C_out_b(fulladder_17_c_out_b), .S_b(fulladder_1_s_b[16]));
  not not_17 (not_17_out, fulladder_17_c_out_b);
  fulladder fulladder_18 (
    .A(A[17]), .B(xor_18_out), .C_in(not_17_out), .C_out_b(fulladder_18_c_out_b), .S_b(fulladder_1_s_b[17]));
  not not_18 (not_18_out, fulladder_18_c_out_b);
  fulladder fulladder_19 (
    .A(A[18]), .B(xor_19_out), .C_in(not_18_out), .C_out_b(fulladder_19_c_out_b), .S_b(fulladder_1_s_b[18]));
  not not_19 (not_19_out, fulladder_19_c_out_b);
  fulladder fulladder_20 (
    .A(A[19]), .B(xor_20_out), .C_in(not_19_out), .C_out_b(fulladder_20_c_out_b), .S_b(fulladder_1_s_b[19]));
  not not_20 (not_20_out, fulladder_20_c_out_b);
  fulladder fulladder_21 (
    .A(A[20]), .B(xor_21_out), .C_in(not_20_out), .C_out_b(fulladder_21_c_out_b), .S_b(fulladder_1_s_b[20]));
  not not_21 (not_21_out, fulladder_21_c_out_b);
  fulladder fulladder_22 (
    .A(A[21]), .B(xor_22_out), .C_in(not_21_out), .C_out_b(fulladder_22_c_out_b), .S_b(fulladder_1_s_b[21]));
  not not_22 (not_22_out, fulladder_22_c_out_b);
  fulladder fulladder_23 (
    .A(A[22]), .B(xor_23_out), .C_in(not_22_out), .C_out_b(fulladder_23_c_out_b), .S_b(fulladder_1_s_b[22]));
  not not_23 (not_23_out, fulladder_23_c_out_b);
  fulladder fulladder_24 (
    .A(A[23]), .B(xor_24_out), .C_in(not_23_out), .C_out_b(fulladder_24_c_out_b), .S_b(fulladder_1_s_b[23]));
  not not_24 (not_24_out, fulladder_24_c_out_b);
  fulladder fulladder_25 (
    .A(A[24]), .B(xor_25_out), .C_in(not_24_out), .C_out_b(fulladder_25_c_out_b), .S_b(fulladder_1_s_b[24]));
  not not_25 (not_25_out, fulladder_25_c_out_b);
  fulladder fulladder_26 (
    .A(A[25]), .B(xor_26_out), .C_in(not_25_out), .C_out_b(fulladder_26_c_out_b), .S_b(fulladder_1_s_b[25]));
  not not_26 (not_26_out, fulladder_26_c_out_b);
  fulladder fulladder_27 (
    .A(A[26]), .B(xor_27_out), .C_in(not_26_out), .C_out_b(fulladder_27_c_out_b), .S_b(fulladder_1_s_b[26]));
  not not_27 (not_27_out, fulladder_27_c_out_b);
  fulladder fulladder_28 (
    .A(A[27]), .B(xor_28_out), .C_in(not_27_out), .C_out_b(fulladder_28_c_out_b), .S_b(fulladder_1_s_b[27]));
  not not_28 (not_28_out, fulladder_28_c_out_b);
  fulladder fulladder_29 (
    .A(A[28]), .B(xor_29_out), .C_in(not_28_out), .C_out_b(fulladder_29_c_out_b), .S_b(fulladder_1_s_b[28]));
  not not_29 (not_29_out, fulladder_29_c_out_b);
  fulladder fulladder_30 (
    .A(A[29]), .B(xor_30_out), .C_in(not_29_out), .C_out_b(fulladder_30_c_out_b), .S_b(fulladder_1_s_b[29]));
  not not_30 (not_30_out, fulladder_30_c_out_b);
  fulladder fulladder_31 (
    .A(A[30]), .B(xor_31_out), .C_in(not_30_out), .C_out_b(fulladder_31_c_out_b), .S_b(fulladder_1_s_b[30]));
  not not_31 (not_31_out, fulladder_31_c_out_b);
  fulladder fulladder_32 (
    .A(A[31]), .B(xor_32_out), .C_in(not_31_out), .C_out_b(fulladder_32_c_out_b), .S_b(fulladder_1_s_b[31]));
  not not_32 (not_32_out, fulladder_32_c_out_b);
  assign not_33_out = ~fulladder_1_s_b;  // NOT_Gate not_33, 32 bits wide
  xor xor_33 (xor_33_out, not_32_out, k);
endmodule

module ALU (
);

  wire add_sub_1_overflow;
  wire [31:0] add_sub_1_y;

  add_sub add_sub_1 (.Overflow(add_sub_1_overflow), .Y(add_sub_1_y));  // open: A, B, k, en_b
endmodule
