// Logisim project BaseParts.circ as structural Verilog: 23 circuits, main circuit dflipflop
module dflipflop (
  input  set_b,
  input  rst_b,
  input  clk,
  input  D,
  output Q,
  output Q_b
);

  wire nand_1_out, nand_2_out, nand_3_out, nand_4_out, not_1_out, not_2_out;

  not not_1 (not_1_out, set_b);
  not not_2 (not_2_out, rst_b);
  nand nand_1 (nand_1_out, not_1_out, nand_4_out, nand_2_out);
  nand nand_2 (nand_2_out, nand_1_out, not_2_out, clk);
  nand nand_3 (nand_3_out, nand_2_out, clk, nand_4_out);
  nand nand_4 (nand_4_out, nand_3_out, not_2_out, D);
  nand nand_5 (Q, not_1_out, nand_2_out, Q_b);
  nand nand_6 (Q_b, Q, not_2_out, nand_3_out);

  // Notes on the sheet:
  //   rst_b: initial=0x1
  //   set_b: initial=0x1
endmodule

module buf1bit (
  input  en_b,
  input  A,
  output Y
);

  wire transistor_1_out;

  Transistor transistor_1 (.in(1'b1), .out(transistor_1_out), .gate(en_b));
  Transistor #(.\type ("n")) transistor_2 (.in(1'b0), .out(transistor_1_out), .gate(en_b));
  Transistor transistor_3 (.in(A), .out(Y), .gate(en_b));
  Transistor #(.\type ("n")) transistor_4 (.in(A), .out(Y), .gate(transistor_1_out));
endmodule

module buf8bit (
  input  [7:0] A,
  input  en_b,
  output [7:0] Y
);

  buf1bit buf1bit_1 (.en_b(en_b), .A(A[0]), .Y(Y[0]));
  buf1bit buf1bit_2 (.en_b(en_b), .A(A[1]), .Y(Y[1]));
  buf1bit buf1bit_3 (.en_b(en_b), .A(A[2]), .Y(Y[2]));
  buf1bit buf1bit_4 (.en_b(en_b), .A(A[3]), .Y(Y[3]));
  buf1bit buf1bit_5 (.en_b(en_b), .A(A[4]), .Y(Y[4]));
  buf1bit buf1bit_6 (.en_b(en_b), .A(A[5]), .Y(Y[5]));
  buf1bit buf1bit_7 (.en_b(en_b), .A(A[6]), .Y(Y[6]));
  buf1bit buf1bit_8 (.en_b(en_b), .A(A[7]), .Y(Y[7]));
endmodule

module buf32bit (
  input  [31:0] A,
  input  en_b,
  output [31:0] Y
);

  buf8bit buf8bit_1 (.A(A[7:0]), .en_b(en_b), .Y(Y[7:0]));
  buf8bit buf8bit_2 (.A(A[15:8]), .en_b(en_b), .Y(Y[15:8]));
  buf8bit buf8bit_3 (.A(A[23:16]), .en_b(en_b), .Y(Y[23:16]));
  buf8bit buf8bit_4 (.A(A[31:24]), .en_b(en_b), .Y(Y[31:24]));
endmodule

module reg8bit (
  input  clk,
  input  rst,
  input  [7:0] D,
  output [7:0] Q
);

  dflipflop dflipflop_1 (.rst_b(rst), .clk(clk), .D(D[0]), .Q(Q[0]));  // open: set_b, Q_b
  dflipflop dflipflop_2 (.rst_b(rst), .clk(clk), .D(D[1]), .Q(Q[1]));  // open: set_b, Q_b
  dflipflop dflipflop_3 (.rst_b(rst), .clk(clk), .D(D[2]), .Q(Q[2]));  // open: set_b, Q_b
  dflipflop dflipflop_4 (.rst_b(rst), .clk(clk), .D(D[3]), .Q(Q[3]));  // open: set_b, Q_b
  dflipflop dflipflop_5 (.rst_b(rst), .clk(clk), .D(D[4]), .Q(Q[4]));  // open: set_b, Q_b
  dflipflop dflipflop_6 (.rst_b(rst), .clk(clk), .D(D[5]), .Q(Q[5]));  // open: set_b, Q_b
  dflipflop dflipflop_7 (.rst_b(rst), .clk(clk), .D(D[6]), .Q(Q[6]));  // open: set_b, Q_b
  dflipflop dflipflop_8 (.rst_b(rst), .clk(clk), .D(D[7]), .Q(Q[7]));  // open: set_b, Q_b
endmodule

module reg16bit (
  input  clk,
  input  rst,
  input  [15:0] D,
  output [15:0] Q
);

  reg8bit reg8bit_1 (.D(D[7:0]), .clk(clk), .rst(rst), .Q(Q[7:0]));
  reg8bit reg8bit_2 (.D(D[15:8]), .clk(clk), .rst(rst), .Q(Q[15:8]));
endmodule

module reg32bit (
  input  clk,
  input  rst,
  input  [31:0] D,
  output [31:0] Q
);

  reg16bit reg16bit_1 (.D(D[15:0]), .clk(clk), .rst(rst), .Q(Q[15:0]));
  reg16bit reg16bit_2 (.D(D[31:16]), .clk(clk), .rst(rst), .Q(Q[31:16]));
endmodule

module mux2to1 (
  input  A,
  input  sel,
  input  B,
  output Y
);

  wire transmission_1_p3;

  // Transmission_Gate transmission_1: pin names not known; wires that end beside it: A, sel, transmission_1_p3, Y
  not not_1 (transmission_1_p3, sel);
  // Transmission_Gate transmission_2: pin names not known; wires that end beside it: B, transmission_1_p3, sel, Y
endmodule

module mux3to1 (
  input  A,
  input  sel_0,
  input  B,
  input  sel_1,
  input  C,
  output out_6
);

  wire not_2_out, transmission_1_p3, transmission_1_p4;

  // Transmission_Gate transmission_1: pin names not known; wires that end beside it: A, sel_0, transmission_1_p3, transmission_1_p4
  not not_1 (transmission_1_p3, sel_0);
  // Transmission_Gate transmission_2: pin names not known; wires that end beside it: B, transmission_1_p3, sel_0, transmission_1_p4
  not not_2 (not_2_out, sel_1);
  // Transmission_Gate transmission_3: pin names not known; wires that end beside it: transmission_1_p4, sel_1, not_2_out, out_6
  // Transmission_Gate transmission_4: pin names not known; wires that end beside it: C, not_2_out, sel_1, out_6
endmodule

module mux4to1 (
  input  A,
  input  sel_0,
  input  B,
  input  sel_1,
  input  C,
  input  D,
  output out_7
);

  wire not_3_out, transmission_1_p3, transmission_1_p4, transmission_3_p3, transmission_3_p4;

  // Transmission_Gate transmission_1: pin names not known; wires that end beside it: A, sel_0, transmission_1_p3, transmission_1_p4
  not not_1 (transmission_1_p3, sel_0);
  // Transmission_Gate transmission_2: pin names not known; wires that end beside it: B, transmission_1_p3, sel_0, transmission_1_p4
  // Transmission_Gate transmission_3: pin names not known; wires that end beside it: C, sel_0, transmission_3_p3, transmission_3_p4
  not not_2 (transmission_3_p3, sel_0);
  // Transmission_Gate transmission_4: pin names not known; wires that end beside it: D, transmission_3_p3, sel_0, transmission_3_p4
  not not_3 (not_3_out, sel_1);
  // Transmission_Gate transmission_5: pin names not known; wires that end beside it: transmission_1_p4, sel_1, not_3_out, out_7
  // Transmission_Gate transmission_6: pin names not known; wires that end beside it: transmission_3_p4, not_3_out, sel_1, out_7
endmodule

module mux2to1_8bit (
  input  [7:0] A,
  input  [7:0] B,
  input  sel,
  output [7:0] Y
);

  mux2to1 mux2to1_1 (.sel(sel), .A(A[0]), .B(B[0]), .Y(Y[0]));
  mux2to1 mux2to1_2 (.sel(sel), .A(A[1]), .B(B[1]), .Y(Y[1]));
  mux2to1 mux2to1_3 (.sel(sel), .A(A[2]), .B(B[2]), .Y(Y[2]));
  mux2to1 mux2to1_4 (.sel(sel), .A(A[3]), .B(B[3]), .Y(Y[3]));
  mux2to1 mux2to1_5 (.sel(sel), .A(A[4]), .B(B[4]), .Y(Y[4]));
  mux2to1 mux2to1_6 (.sel(sel), .A(A[5]), .B(B[5]), .Y(Y[5]));
  mux2to1 mux2to1_7 (.sel(sel), .A(A[6]), .B(B[6]), .Y(Y[6]));
  mux2to1 mux2to1_8 (.sel(sel), .A(A[7]), .B(B[7]), .Y(Y[7]));
endmodule

module mux2to1_16bit (
  input  [15:0] A,
  input  [15:0] B,
  input  sel,
  output [15:0] Y
);

  mux2to1_8bit mux2to1_8bit_1 (.B(B[7:0]), .A(A[7:0]), .sel(sel), .Y(Y[7:0]));
  mux2to1_8bit mux2to1_8bit_2 (.B(B[15:8]), .A(A[15:8]), .sel(sel), .Y(Y[15:8]));
endmodule

module mux2to1_32bit (
  input  [31:0] A,
  input  [31:0] B,
  input  sel,
  output [31:0] Y
);

  mux2to1_16bit mux2to1_16bit_1 (.B(B[15:0]), .A(A[15:0]), .sel(sel), .Y(Y[15:0]));
  mux2to1_16bit mux2to1_16bit_2 (.B(B[31:16]), .A(A[31:16]), .sel(sel), .Y(Y[31:16]));
endmodule

module regwith2to1mux8bit (
  input  clk,
  input  rst,
  input  [7:0] D,
  input  en,
  output [7:0] Q
);

  wire [7:0] mux2to1_8bit_1_y;

  mux2to1_8bit mux2to1_8bit_1 (.B(D), .A(Q), .sel(en), .Y(mux2to1_8bit_1_y));
  reg8bit reg8bit_1 (.D(mux2to1_8bit_1_y), .clk(clk), .rst(rst), .Q(Q));
endmodule

module regwith2to1mux32bit (
  input  clk,
  input  rst,
  input  [31:0] D,
  input  en,
  output [31:0] Q
);

  wire [31:0] mux2to1_32bit_1_y;

  mux2to1_32bit mux2to1_32bit_1 (.B(D), .A(Q), .sel(en), .Y(mux2to1_32bit_1_y));
  reg32bit reg32bit_1 (.D(mux2to1_32bit_1_y), .clk(clk), .rst(rst), .Q(Q));
endmodule

module decoder2to4 (
  input  en_b,
  input  A1,
  input  A0,
  output Y0,
  output Y1,
  output Y2,
  output Y3
);

  wire not_1_out, not_2_out, not_3_out;

  not not_1 (not_1_out, en_b);
  not not_2 (not_2_out, A1);
  not not_3 (not_3_out, A0);
  and and_1 (Y0, not_3_out, not_2_out, not_1_out);
  and and_2 (Y1, not_2_out, A0, not_1_out);
  and and_3 (Y2, A1, not_3_out, not_1_out);
  and and_4 (Y3, A1, A0, not_1_out);
endmodule

module decoder2to4INV (
  input  en_b,
  input  A1,
  input  A0,
  output Y0,
  output Y1,
  output Y2,
  output Y3
);

  wire not_1_out, not_2_out, not_3_out;

  not not_1 (not_1_out, en_b);
  not not_2 (not_2_out, A1);
  not not_3 (not_3_out, A0);
  nand nand_1 (Y0, not_3_out, not_2_out, not_1_out);
  nand nand_2 (Y1, not_2_out, A0, not_1_out);
  nand nand_3 (Y2, not_3_out, A1, not_1_out);
  nand nand_4 (Y3, A0, A1, not_1_out);
endmodule

module decoder3to8 (
  input  A2,
  input  A0,
  input  A1,
  input  en_b,
  output Y0,
  output Y1,
  output Y2,
  output Y3,
  output Y4,
  output Y5,
  output Y6,
  output Y7
);

  wire not_1_out, or_1_out, or_2_out;

  not not_1 (not_1_out, A2);
  or or_1 (or_1_out, A2, en_b);
  or or_2 (or_2_out, not_1_out, en_b);
  decoder2to4 decoder2to4_1 (.en_b(or_1_out), .A1(A1), .A0(A0), .Y0(Y0), .Y1(Y1), .Y2(Y2), .Y3(Y3));
  decoder2to4 decoder2to4_2 (.en_b(or_2_out), .A1(A1), .A0(A0), .Y0(Y4), .Y1(Y5), .Y2(Y6), .Y3(Y7));
endmodule

module decoder3to8INV (
  input  A2,
  input  A0,
  input  A1,
  input  en_b,
  output Y0,
  output Y1,
  output Y2,
  output Y3,
  output Y4,
  output Y5,
  output Y6,
  output Y7
);

  wire not_1_out, or_1_out, or_2_out;

  not not_1 (not_1_out, A2);
  or or_1 (or_1_out, A2, en_b);
  or or_2 (or_2_out, not_1_out, en_b);
  decoder2to4INV decoder2to4inv_1 (.en_b(or_1_out), .A1(A1), .A0(A0), .Y0(Y0), .Y1(Y1), .Y2(Y2), .Y3(Y3));
  decoder2to4INV decoder2to4inv_2 (.en_b(or_2_out), .A1(A1), .A0(A0), .Y0(Y4), .Y1(Y5), .Y2(Y6), .Y3(Y7));
endmodule

module decoder4to16 (
  input  A3,
  input  en_b,
  input  A0,
  input  A1,
  input  A2,
  output Y_0,
  output Y_1,
  output Y_2,
  output Y_3,
  output Y_4,
  output Y_5,
  output Y_6,
  output Y_7,
  output Y_8,
  output Y_9,
  output Y_10,
  output Y_11,
  output Y_12,
  output Y_13,
  output Y_14,
  output Y_15
);

  wire not_1_out, or_1_out, or_2_out;

  or or_1 (or_1_out, A3, en_b);
  not not_1 (not_1_out, A3);
  or or_2 (or_2_out, not_1_out, en_b);
  decoder3to8 decoder3to8_1 (
    .A2(A2), .A0(A0), .A1(A1), .en_b(or_1_out), .Y0(Y_0), .Y3(Y_3), .Y2(Y_2), .Y4(Y_4), .Y5(Y_5), .Y6(Y_6),
    .Y7(Y_7), .Y1(Y_1));
  decoder3to8 decoder3to8_2 (
    .A2(A2), .A0(A0), .A1(A1), .en_b(or_2_out), .Y0(Y_8), .Y3(Y_11), .Y2(Y_10), .Y4(Y_12), .Y5(Y_13),
    .Y6(Y_14), .Y7(Y_15), .Y1(Y_9));
endmodule

module decoder4to16INV (
  input  A3,
  input  en_b,
  input  A0,
  input  A1,
  input  A2,
  output Y_0,
  output Y_1,
  output Y_2,
  output Y_3,
  output Y_4,
  output Y_5,
  output Y_6,
  output Y_7,
  output Y_8,
  output Y_9,
  output Y_10,
  output Y_11,
  output Y_12,
  output Y_13,
  output Y_14,
  output Y_15
);

  wire not_1_out, or_1_out, or_2_out;

  or or_1 (or_1_out, A3, en_b);
  not not_1 (not_1_out, A3);
  or or_2 (or_2_out, not_1_out, en_b);
  decoder3to8INV decoder3to8inv_1 (
    .A2(A2), .A0(A0), .A1(A1), .en_b(or_1_out), .Y0(Y_0), .Y3(Y_3), .Y2(Y_2), .Y4(Y_4), .Y5(Y_5), .Y6(Y_6),
    .Y7(Y_7), .Y1(Y_1));
  decoder3to8INV decoder3to8inv_2 (
    .A2(A2), .A0(A0), .A1(A1), .en_b(or_2_out), .Y0(Y_8), .Y3(Y_11), .Y2(Y_10), .Y4(Y_12), .Y5(Y_13),
    .Y6(Y_14), .Y7(Y_15), .Y1(Y_9));
endmodule

module decoder5to32 (
  input  en_b,
  input  A4,
  input  A0,
  input  A1,
  input  A2,
  input  A3,
  output Y,
  output Y_1,
  output Y_2,
  output Y_3,
  output Y_4,
  output Y_5,
  output Y_6,
  output Y_7,
  output Y_8,
  output Y_9,
  output Y_10,
  output Y_11,
  output Y_12,
  output Y_13,
  output Y_14,
  output Y_15,
  output Y_16,
  output Y_17,
  output Y_18,
  output Y_19,
  output Y_20,
  output Y_21,
  output Y_22,
  output Y_23,
  output Y_24,
  output Y_25,
  output Y_26,
  output Y_27,
  output Y_28,
  output Y_29,
  output Y_30,
  output Y_31
);

  wire not_1_out, or_1_out, or_2_out;

  or or_1 (or_1_out, A4, en_b);
  not not_1 (not_1_out, A4);
  or or_2 (or_2_out, not_1_out, en_b);
  decoder4to16 decoder4to16_1 (
    .A2(A2), .A0(A0), .A1(A1), .en_b(or_1_out), .A3(A3), .Y_0(Y), .Y_1(Y_1), .Y_2(Y_2), .Y_3(Y_3), .Y_4(Y_4),
    .Y_5(Y_5), .Y_6(Y_6), .Y_7(Y_7), .Y_8(Y_8), .Y_9(Y_9), .Y_10(Y_10), .Y_11(Y_11), .Y_12(Y_12),
    .Y_13(Y_13), .Y_14(Y_14), .Y_15(Y_15));
  decoder4to16 decoder4to16_2 (
    .A2(A2), .A0(A0), .A1(A1), .en_b(or_2_out), .A3(A3), .Y_0(Y_16), .Y_1(Y_17), .Y_2(Y_18), .Y_3(Y_19),
    .Y_4(Y_20), .Y_5(Y_21), .Y_6(Y_22), .Y_7(Y_23), .Y_8(Y_24), .Y_9(Y_25), .Y_10(Y_26), .Y_11(Y_27),
    .Y_12(Y_28), .Y_13(Y_29), .Y_14(Y_30), .Y_15(Y_31));
endmodule

module decoder5to32INV (
  input  en_b,
  input  A4,
  input  A0,
  input  A1,
  input  A2,
  input  A3,
  output Y,
  output Y_1,
  output Y_2,
  output Y_3,
  output Y_4,
  output Y_5,
  output Y_6,
  output Y_7,
  output Y_8,
  output Y_9,
  output Y_10,
  output Y_11,
  output Y_12,
  output Y_13,
  output Y_14,
  output Y_15,
  output Y_16,
  output Y_17,
  output Y_18,
  output Y_19,
  output Y_20,
  output Y_21,
  output Y_22,
  output Y_23,
  output Y_24,
  output Y_25,
  output Y_26,
  output Y_27,
  output Y_28,
  output Y_29,
  output Y_30,
  output Y_31
);

  wire not_1_out, or_1_out, or_2_out;

  or or_1 (or_1_out, A4, en_b);
  not not_1 (not_1_out, A4);
  or or_2 (or_2_out, not_1_out, en_b);
  decoder4to16INV decoder4to16inv_1 (
    .A2(A2), .A0(A0), .A1(A1), .en_b(or_1_out), .A3(A3), .Y_0(Y), .Y_1(Y_1), .Y_2(Y_2), .Y_3(Y_3), .Y_4(Y_4),
    .Y_5(Y_5), .Y_6(Y_6), .Y_7(Y_7), .Y_8(Y_8), .Y_9(Y_9), .Y_10(Y_10), .Y_11(Y_11), .Y_12(Y_12),
    .Y_13(Y_13), .Y_14(Y_14), .Y_15(Y_15));
  decoder4to16INV decoder4to16inv_2 (
    .A2(A2), .A0(A0), .A1(A1), .en_b(or_2_out), .A3(A3), .Y_0(Y_16), .Y_1(Y_17), .Y_2(Y_18), .Y_3(Y_19),
    .Y_4(Y_20), .Y_5(Y_21), .Y_6(Y_22), .Y_7(Y_23), .Y_8(Y_24), .Y_9(Y_25), .Y_10(Y_26), .Y_11(Y_27),
    .Y_12(Y_28), .Y_13(Y_29), .Y_14(Y_30), .Y_15(Y_31));
endmodule
