// Logisim project RegisterFile.circ as structural Verilog
module regbyte (
  input  [31:0] D,
  input  [3:0] write_reg_byte,
  input  write_reg,
  input  clk,
  input  rst,
  input  A_en_b,
  input  B_en_b,
  output [31:0] Q,
  output [31:0] A,
  output [31:0] B
);

  wire or_1_out, or_2_out, or_3_out, or_4_out;

  // Probe on write_reg_byte
  // Probe on write_reg_byte[0]
  // Probe on write_reg_byte[1]
  // Probe on write_reg_byte[2]
  // Probe on write_reg_byte[3]
  or or_1 (or_1_out, write_reg, write_reg_byte[0]);
  or or_2 (or_2_out, write_reg, write_reg_byte[1]);
  or or_3 (or_3_out, write_reg, write_reg_byte[2]);
  or or_4 (or_4_out, write_reg, write_reg_byte[3]);
  regwith2to1mux8bit regwith2to1mux8bit_1 (.D(D[7:0]), .en(or_1_out), .clk(clk), .rst(rst), .Q(Q[7:0]));
  regwith2to1mux8bit regwith2to1mux8bit_2 (.D(D[15:8]), .en(or_2_out), .clk(clk), .rst(rst), .Q(Q[15:8]));
  regwith2to1mux8bit regwith2to1mux8bit_3 (.D(D[23:16]), .en(or_3_out), .clk(clk), .rst(rst), .Q(Q[23:16]));
  regwith2to1mux8bit regwith2to1mux8bit_4 (.D(D[31:24]), .en(or_4_out), .clk(clk), .rst(rst), .Q(Q[31:24]));
  buf32bit buf32bit_1 (.A(Q), .en_b(A_en_b), .Y(A));
  buf32bit buf32bit_2 (.A(Q), .en_b(B_en_b), .Y(B));
endmodule

module regzero (
  input  clk,
  input  [31:0] D,
  input  A_en_b,
  input  B_en_b,
  output [31:0] Q,
  output [31:0] A,
  output [31:0] B
);

  buf32bit buf32bit_1 (.A({32{1'b0}}), .en_b(A_en_b), .Y(A));
  buf32bit buf32bit_2 (.A({32{1'b0}}), .en_b(B_en_b), .Y(B));

  assign Q = {32{1'b0}};
endmodule

module RegFile (
  input  [4:0] A_read_addr,
  input  [4:0] B_read_addr,
  input  [3:0] write_reg_byte,
  input  clk,
  input  rst,
  input  [5:0] write_address,
  input  [31:0] C,
  output [31:0] A,
  output [31:0] B
);

  wire [31:0] decoder5to32_1_y, decoder5to32inv_1_y, decoder5to32inv_2_y, regbyte_1_q, regbyte_2_q,
       regbyte_3_q, regbyte_4_q, regbyte_5_q, regbyte_6_q, regbyte_7_q, regbyte_8_q, regbyte_9_q,
       regbyte_10_q, regbyte_11_q, regbyte_12_q, regbyte_13_q, regbyte_14_q, regbyte_15_q, regbyte_16_q,
       regbyte_17_q, regbyte_18_q, regbyte_19_q, regbyte_20_q, regbyte_21_q, regbyte_22_q, regbyte_23_q,
       regbyte_24_q, regbyte_25_q, regbyte_26_q, regbyte_27_q, regbyte_28_q, regbyte_29_q, regbyte_30_q,
       regbyte_31_q, regzero_1_q;

  decoder5to32 decoder5to32_1 (
    .A0(write_address[1]), .A1(write_address[2]), .A2(write_address[3]), .A3(write_address[4]),
    .en_b(write_address[0]), .A4(write_address[5]), .Y(decoder5to32_1_y[0]), .Y_1(decoder5to32_1_y[1]),
    .Y_2(decoder5to32_1_y[2]), .Y_3(decoder5to32_1_y[3]), .Y_4(decoder5to32_1_y[4]),
    .Y_5(decoder5to32_1_y[5]), .Y_6(decoder5to32_1_y[6]), .Y_7(decoder5to32_1_y[7]),
    .Y_8(decoder5to32_1_y[8]), .Y_9(decoder5to32_1_y[9]), .Y_10(decoder5to32_1_y[10]),
    .Y_11(decoder5to32_1_y[11]), .Y_12(decoder5to32_1_y[12]), .Y_13(decoder5to32_1_y[13]),
    .Y_14(decoder5to32_1_y[14]), .Y_15(decoder5to32_1_y[15]), .Y_16(decoder5to32_1_y[16]),
    .Y_17(decoder5to32_1_y[17]), .Y_18(decoder5to32_1_y[18]), .Y_19(decoder5to32_1_y[19]),
    .Y_20(decoder5to32_1_y[20]), .Y_21(decoder5to32_1_y[21]), .Y_22(decoder5to32_1_y[22]),
    .Y_23(decoder5to32_1_y[23]), .Y_24(decoder5to32_1_y[24]), .Y_25(decoder5to32_1_y[25]),
    .Y_26(decoder5to32_1_y[26]), .Y_27(decoder5to32_1_y[27]), .Y_28(decoder5to32_1_y[28]),
    .Y_29(decoder5to32_1_y[29]), .Y_30(decoder5to32_1_y[30]), .Y_31(decoder5to32_1_y[31]));
  decoder5to32INV decoder5to32inv_1 (
    .A0(B_read_addr[0]), .A1(B_read_addr[1]), .A2(B_read_addr[2]), .A3(B_read_addr[3]), .en_b(1'b0),
    .A4(B_read_addr[4]), .Y(decoder5to32inv_1_y[0]), .Y_1(decoder5to32inv_1_y[1]),
    .Y_2(decoder5to32inv_1_y[2]), .Y_3(decoder5to32inv_1_y[3]), .Y_4(decoder5to32inv_1_y[4]),
    .Y_5(decoder5to32inv_1_y[5]), .Y_6(decoder5to32inv_1_y[6]), .Y_7(decoder5to32inv_1_y[7]),
    .Y_8(decoder5to32inv_1_y[8]), .Y_9(decoder5to32inv_1_y[9]), .Y_10(decoder5to32inv_1_y[10]),
    .Y_11(decoder5to32inv_1_y[11]), .Y_12(decoder5to32inv_1_y[12]), .Y_13(decoder5to32inv_1_y[13]),
    .Y_14(decoder5to32inv_1_y[14]), .Y_15(decoder5to32inv_1_y[15]), .Y_16(decoder5to32inv_1_y[16]),
    .Y_17(decoder5to32inv_1_y[17]), .Y_18(decoder5to32inv_1_y[18]), .Y_19(decoder5to32inv_1_y[19]),
    .Y_20(decoder5to32inv_1_y[20]), .Y_21(decoder5to32inv_1_y[21]), .Y_22(decoder5to32inv_1_y[22]),
    .Y_23(decoder5to32inv_1_y[23]), .Y_24(decoder5to32inv_1_y[24]), .Y_25(decoder5to32inv_1_y[25]),
    .Y_26(decoder5to32inv_1_y[26]), .Y_27(decoder5to32inv_1_y[27]), .Y_28(decoder5to32inv_1_y[28]),
    .Y_29(decoder5to32inv_1_y[29]), .Y_30(decoder5to32inv_1_y[30]), .Y_31(decoder5to32inv_1_y[31]));
  decoder5to32INV decoder5to32inv_2 (
    .A0(A_read_addr[0]), .A1(A_read_addr[1]), .A2(A_read_addr[2]), .A3(A_read_addr[3]), .en_b(1'b0),
    .A4(A_read_addr[4]), .Y(decoder5to32inv_2_y[0]), .Y_1(decoder5to32inv_2_y[1]),
    .Y_2(decoder5to32inv_2_y[2]), .Y_3(decoder5to32inv_2_y[3]), .Y_4(decoder5to32inv_2_y[4]),
    .Y_5(decoder5to32inv_2_y[5]), .Y_6(decoder5to32inv_2_y[6]), .Y_7(decoder5to32inv_2_y[7]),
    .Y_8(decoder5to32inv_2_y[8]), .Y_9(decoder5to32inv_2_y[9]), .Y_10(decoder5to32inv_2_y[10]),
    .Y_11(decoder5to32inv_2_y[11]), .Y_12(decoder5to32inv_2_y[12]), .Y_13(decoder5to32inv_2_y[13]),
    .Y_14(decoder5to32inv_2_y[14]), .Y_15(decoder5to32inv_2_y[15]), .Y_16(decoder5to32inv_2_y[16]),
    .Y_17(decoder5to32inv_2_y[17]), .Y_18(decoder5to32inv_2_y[18]), .Y_19(decoder5to32inv_2_y[19]),
    .Y_20(decoder5to32inv_2_y[20]), .Y_21(decoder5to32inv_2_y[21]), .Y_22(decoder5to32inv_2_y[22]),
    .Y_23(decoder5to32inv_2_y[23]), .Y_24(decoder5to32inv_2_y[24]), .Y_25(decoder5to32inv_2_y[25]),
    .Y_26(decoder5to32inv_2_y[26]), .Y_27(decoder5to32inv_2_y[27]), .Y_28(decoder5to32inv_2_y[28]),
    .Y_29(decoder5to32inv_2_y[29]), .Y_30(decoder5to32inv_2_y[30]), .Y_31(decoder5to32inv_2_y[31]));
  // Probe on write_reg_byte
  regbyte regbyte_1 (
    .write_reg_byte(write_reg_byte), .write_reg(decoder5to32_1_y[0]), .D(C), .clk(clk), .rst(rst),
    .A_en_b(decoder5to32inv_2_y[0]), .B_en_b(decoder5to32inv_1_y[0]), .Q(regbyte_1_q), .A(A), .B(B));
  regbyte regbyte_2 (
    .write_reg_byte(write_reg_byte), .write_reg(decoder5to32_1_y[1]), .D(C), .clk(clk), .rst(rst),
    .A_en_b(decoder5to32inv_2_y[1]), .B_en_b(decoder5to32inv_1_y[1]), .Q(regbyte_2_q), .A(A), .B(B));
  regbyte regbyte_3 (
    .write_reg_byte(write_reg_byte), .write_reg(decoder5to32_1_y[2]), .D(C), .clk(clk), .rst(rst),
    .A_en_b(decoder5to32inv_2_y[2]), .B_en_b(decoder5to32inv_1_y[2]), .Q(regbyte_3_q), .A(A), .B(B));
  regbyte regbyte_4 (
    .write_reg_byte(write_reg_byte), .write_reg(decoder5to32_1_y[3]), .D(C), .clk(clk), .rst(rst),
    .A_en_b(decoder5to32inv_2_y[3]), .B_en_b(decoder5to32inv_1_y[3]), .Q(regbyte_4_q), .A(A), .B(B));
  regbyte regbyte_5 (
    .write_reg_byte(write_reg_byte), .write_reg(decoder5to32_1_y[4]), .D(C), .clk(clk), .rst(rst),
    .A_en_b(decoder5to32inv_2_y[4]), .B_en_b(decoder5to32inv_1_y[4]), .Q(regbyte_5_q), .A(A), .B(B));
  regbyte regbyte_6 (
    .write_reg_byte(write_reg_byte), .write_reg(decoder5to32_1_y[5]), .D(C), .clk(clk), .rst(rst),
    .A_en_b(decoder5to32inv_2_y[5]), .B_en_b(decoder5to32inv_1_y[5]), .Q(regbyte_6_q), .A(A), .B(B));
  regbyte regbyte_7 (
    .write_reg_byte(write_reg_byte), .write_reg(decoder5to32_1_y[6]), .D(C), .clk(clk), .rst(rst),
    .A_en_b(decoder5to32inv_2_y[6]), .B_en_b(decoder5to32inv_1_y[6]), .Q(regbyte_7_q), .A(A), .B(B));
  regbyte regbyte_8 (
    .write_reg_byte(write_reg_byte), .write_reg(decoder5to32_1_y[7]), .D(C), .clk(clk), .rst(rst),
    .A_en_b(decoder5to32inv_2_y[7]), .B_en_b(decoder5to32inv_1_y[7]), .Q(regbyte_8_q), .A(A), .B(B));
  regbyte regbyte_9 (
    .write_reg_byte(write_reg_byte), .write_reg(decoder5to32_1_y[8]), .D(C), .clk(clk), .rst(rst),
    .A_en_b(decoder5to32inv_2_y[8]), .B_en_b(decoder5to32inv_1_y[8]), .Q(regbyte_9_q), .A(A), .B(B));
  regbyte regbyte_10 (
    .write_reg_byte(write_reg_byte), .write_reg(decoder5to32_1_y[9]), .D(C), .clk(clk), .rst(rst),
    .A_en_b(decoder5to32inv_2_y[9]), .B_en_b(decoder5to32inv_1_y[9]), .Q(regbyte_10_q), .A(A), .B(B));
  regbyte regbyte_11 (
    .write_reg_byte(write_reg_byte), .write_reg(decoder5to32_1_y[10]), .D(C), .clk(clk), .rst(rst),
    .A_en_b(decoder5to32inv_2_y[10]), .B_en_b(decoder5to32inv_1_y[10]), .Q(regbyte_11_q), .A(A), .B(B));
  regbyte regbyte_12 (
    .write_reg_byte(write_reg_byte), .write_reg(decoder5to32_1_y[11]), .D(C), .clk(clk), .rst(rst),
    .A_en_b(decoder5to32inv_2_y[11]), .B_en_b(decoder5to32inv_1_y[11]), .Q(regbyte_12_q), .A(A), .B(B));
  regbyte regbyte_13 (
    .write_reg_byte(write_reg_byte), .write_reg(decoder5to32_1_y[12]), .D(C), .clk(clk), .rst(rst),
    .A_en_b(decoder5to32inv_2_y[12]), .B_en_b(decoder5to32inv_1_y[12]), .Q(regbyte_13_q), .A(A), .B(B));
  regbyte regbyte_14 (
    .write_reg_byte(write_reg_byte), .write_reg(decoder5to32_1_y[13]), .D(C), .clk(clk), .rst(rst),
    .A_en_b(decoder5to32inv_2_y[13]), .B_en_b(decoder5to32inv_1_y[13]), .Q(regbyte_14_q), .A(A), .B(B));
  regbyte regbyte_15 (
    .write_reg_byte(write_reg_byte), .write_reg(decoder5to32_1_y[14]), .D(C), .clk(clk), .rst(rst),
    .A_en_b(decoder5to32inv_2_y[14]), .B_en_b(decoder5to32inv_1_y[14]), .Q(regbyte_15_q), .A(A), .B(B));
  regbyte regbyte_16 (
    .write_reg_byte(write_reg_byte), .write_reg(decoder5to32_1_y[15]), .D(C), .clk(clk), .rst(rst),
    .A_en_b(decoder5to32inv_2_y[15]), .B_en_b(decoder5to32inv_1_y[15]), .Q(regbyte_16_q), .A(A), .B(B));
  regbyte regbyte_17 (
    .write_reg_byte(write_reg_byte), .write_reg(decoder5to32_1_y[16]), .D(C), .clk(clk), .rst(rst),
    .A_en_b(decoder5to32inv_2_y[16]), .B_en_b(decoder5to32inv_1_y[16]), .Q(regbyte_17_q), .A(A), .B(B));
  regbyte regbyte_18 (
    .write_reg_byte(write_reg_byte), .write_reg(decoder5to32_1_y[17]), .D(C), .clk(clk), .rst(rst),
    .A_en_b(decoder5to32inv_2_y[17]), .B_en_b(decoder5to32inv_1_y[17]), .Q(regbyte_18_q), .A(A), .B(B));
  regbyte regbyte_19 (
    .write_reg_byte(write_reg_byte), .write_reg(decoder5to32_1_y[18]), .D(C), .clk(clk), .rst(rst),
    .A_en_b(decoder5to32inv_2_y[18]), .B_en_b(decoder5to32inv_1_y[18]), .Q(regbyte_19_q), .A(A), .B(B));
  regbyte regbyte_20 (
    .write_reg_byte(write_reg_byte), .write_reg(decoder5to32_1_y[19]), .D(C), .clk(clk), .rst(rst),
    .A_en_b(decoder5to32inv_2_y[19]), .B_en_b(decoder5to32inv_1_y[19]), .Q(regbyte_20_q), .A(A), .B(B));
  regbyte regbyte_21 (
    .write_reg_byte(write_reg_byte), .write_reg(decoder5to32_1_y[20]), .D(C), .clk(clk), .rst(rst),
    .A_en_b(decoder5to32inv_2_y[20]), .B_en_b(decoder5to32inv_1_y[20]), .Q(regbyte_21_q), .A(A), .B(B));
  regbyte regbyte_22 (
    .write_reg_byte(write_reg_byte), .write_reg(decoder5to32_1_y[21]), .D(C), .clk(clk), .rst(rst),
    .A_en_b(decoder5to32inv_2_y[21]), .B_en_b(decoder5to32inv_1_y[21]), .Q(regbyte_22_q), .A(A), .B(B));
  regbyte regbyte_23 (
    .write_reg_byte(write_reg_byte), .write_reg(decoder5to32_1_y[22]), .D(C), .clk(clk), .rst(rst),
    .A_en_b(decoder5to32inv_2_y[22]), .B_en_b(decoder5to32inv_1_y[22]), .Q(regbyte_23_q), .A(A), .B(B));
  regbyte regbyte_24 (
    .write_reg_byte(write_reg_byte), .write_reg(decoder5to32_1_y[23]), .D(C), .clk(clk), .rst(rst),
    .A_en_b(decoder5to32inv_2_y[23]), .B_en_b(decoder5to32inv_1_y[23]), .Q(regbyte_24_q), .A(A), .B(B));
  regbyte regbyte_25 (
    .write_reg_byte(write_reg_byte), .write_reg(decoder5to32_1_y[24]), .D(C), .clk(clk), .rst(rst),
    .A_en_b(decoder5to32inv_2_y[24]), .B_en_b(decoder5to32inv_1_y[24]), .Q(regbyte_25_q), .A(A), .B(B));
  regbyte regbyte_26 (
    .write_reg_byte(write_reg_byte), .write_reg(decoder5to32_1_y[25]), .D(C), .clk(clk), .rst(rst),
    .A_en_b(decoder5to32inv_2_y[25]), .B_en_b(decoder5to32inv_1_y[25]), .Q(regbyte_26_q), .A(A), .B(B));
  regbyte regbyte_27 (
    .write_reg_byte(write_reg_byte), .write_reg(decoder5to32_1_y[26]), .D(C), .clk(clk), .rst(rst),
    .A_en_b(decoder5to32inv_2_y[26]), .B_en_b(decoder5to32inv_1_y[26]), .Q(regbyte_27_q), .A(A), .B(B));
  regbyte regbyte_28 (
    .write_reg_byte(write_reg_byte), .write_reg(decoder5to32_1_y[27]), .D(C), .clk(clk), .rst(rst),
    .A_en_b(decoder5to32inv_2_y[27]), .B_en_b(decoder5to32inv_1_y[27]), .Q(regbyte_28_q), .A(A), .B(B));
  regbyte regbyte_29 (
    .write_reg_byte(write_reg_byte), .write_reg(decoder5to32_1_y[28]), .D(C), .clk(clk), .rst(rst),
    .A_en_b(decoder5to32inv_2_y[28]), .B_en_b(decoder5to32inv_1_y[28]), .Q(regbyte_29_q), .A(A), .B(B));
  regbyte regbyte_30 (
    .write_reg_byte(write_reg_byte), .write_reg(decoder5to32_1_y[29]), .D(C), .clk(clk), .rst(rst),
    .A_en_b(decoder5to32inv_2_y[29]), .B_en_b(decoder5to32inv_1_y[29]), .Q(regbyte_30_q), .A(A), .B(B));
  regbyte regbyte_31 (
    .write_reg_byte(write_reg_byte), .write_reg(decoder5to32_1_y[30]), .D(C), .clk(clk), .rst(rst),
    .A_en_b(decoder5to32inv_2_y[30]), .B_en_b(decoder5to32inv_1_y[30]), .Q(regbyte_31_q), .A(A), .B(B));
  regzero regzero_1 (
    .D(C), .clk(clk), .A_en_b(decoder5to32inv_2_y[31]), .B_en_b(decoder5to32inv_1_y[31]), .Q(regzero_1_q),
    .A(A), .B(B));
  // Probe on regbyte_1_q
  // Probe on regbyte_2_q
  // Probe on regbyte_3_q
  // Probe on regbyte_4_q
  // Probe on regbyte_5_q
  // Probe on regbyte_6_q
  // Probe on regbyte_7_q
  // Probe on regbyte_8_q
  // Probe on regbyte_9_q
  // Probe on regbyte_10_q
  // Probe on regbyte_11_q
  // Probe on regbyte_12_q
  // Probe on regbyte_13_q
  // Probe on regbyte_14_q
  // Probe on regbyte_15_q
  // Probe on regbyte_16_q
  // Probe on regbyte_17_q
  // Probe on regbyte_18_q
  // Probe on regbyte_19_q
  // Probe on regbyte_20_q
  // Probe on regbyte_21_q
  // Probe on regbyte_22_q
  // Probe on regbyte_23_q
  // Probe on regbyte_24_q
  // Probe on regbyte_25_q
  // Probe on regbyte_26_q
  // Probe on regbyte_27_q
  // Probe on regbyte_28_q
  // Probe on regbyte_29_q
  // Probe on regbyte_30_q
  // Probe on regbyte_31_q
  // Probe on regzero_1_q
endmodule

module test (
  input  [4:0] A_read_address,
  input  [3:0] Byte_write,
  input  [4:0] B_read_address,
  input  [5:0] Write_adress,
  input  [31:0] C,
  input  rst,
  input  clk,
  output [31:0] A,
  output [31:0] B
);

  RegFile regfile_1 (
    .rst(rst), .A_read_addr(A_read_address), .B_read_addr(B_read_address), .write_address(Write_adress),
    .C(C), .write_reg_byte(Byte_write), .clk(clk), .A(A), .B(B));
endmodule
